// Logisim project ALU 32v2.circ as structural Verilog: 1 circuit, main circuit 32 bit ALU
module _32_bit_ALU (
  input  [31:0] in_1,
  input  [31:0] in_2,
  input  [31:0] in_3,
  input  [3:0] in_4,
  output [31:0] out_5
);

  wire [7:0] comparator_1_lt, comparator_2_lt, undriven, undriven_2, undriven_3, undriven_4, undriven_5,
       undriven_6;
  wire [31:0] adder_1_out, and_1_out, or_1_out, shifter_1_out, shifter_2_out, shifter_3_out,
       subtractor_1_out, xor_1_out;

  assign or_1_out = in_2 | in_3;  // OR_Gate or_1, 32 bits wide
  assign and_1_out = in_2 & in_3;  // AND_Gate and_1, 32 bits wide
  assign xor_1_out = in_2 ^ in_3;  // XOR_Gate xor_1, 32 bits wide
  Adder #(.width(32)) adder_1 (.a(in_2), .b(in_3), .out(adder_1_out), .cin(in_1[0]));  // open: cout
  Subtractor #(.width(32)) subtractor_1 (.a(in_2), .b(in_3), .out(subtractor_1_out), .bin(in_1[0]));  // open: bout
  Comparator #(.width(32)) comparator_1 (.a(in_2), .b(in_3), .lt(comparator_1_lt[0]));  // open: gt, eq
  Comparator #(.width(32), .mode("unsigned")) comparator_2 (
    .a(in_2), .b(in_3), .lt(comparator_2_lt[0]));  // open: gt, eq
  Shifter #(.width(32)) shifter_1 (.in(in_2), .\dist (in_3[4:0]), .out(shifter_1_out));
  Shifter #(.width(32), .shift("lr")) shifter_2 (.in(in_2), .\dist (in_3[4:0]), .out(shifter_2_out));
  Shifter #(.width(32), .shift("ar")) shifter_3 (.in(in_2), .\dist (in_3[4:0]), .out(shifter_3_out));
  Multiplexer #(.select(4), .width(32)) multiplexer_1 (
    .in0(adder_1_out), .in1(shifter_1_out), .in2({undriven_3, undriven_2, undriven, comparator_1_lt}),
    .in3({undriven_6, undriven_5, undriven_4, comparator_2_lt}), .in4(xor_1_out), .in5(shifter_2_out),
    .in6(or_1_out), .in7(and_1_out), .in8(subtractor_1_out), .in12(shifter_3_out), .out(out_5), .sel(in_4));  // open: in9, in10, in11, in13, in14, in15, en

  // Notes on the sheet:
  //   OR
  //   And
  //   XOR
  //   ADD
  //   SUB
  //   BLT/SLT
  //   SLTU
  //   SLL
  //   SRL
  //   SRA
endmodule
