// Logisim project ALU32bit.circ as structural Verilog: 3 circuits, main circuit main
module main (
  input  [31:0] in_1,
  input  [31:0] in_2,
  input  [31:0] in_3,
  input  [31:0] in_4,
  input  [31:0] in_5,
  output [31:0] out_6
);

  wire adder_1_cout;
  wire [31:0] adder_1_out, and_1_out, n32bit_comparator_1_out_3, n32bit_comparator_1_out_4,
       n32bit_comparator_1_out_5, or_1_out, or_2_out, subtractor_1_out, xor_1_out;

  Adder #(.width(32)) adder_1 (.a(in_1), .b(in_2), .out(adder_1_out), .cout(adder_1_cout));  // open: cin
  Subtractor #(.width(32)) subtractor_1 (.a(in_1), .b(in_2), .out(subtractor_1_out), .bin(adder_1_cout));  // open: bout
  assign or_1_out = in_1 | in_2;  // OR_Gate or_1, 32 bits wide
  assign and_1_out = in_1 & in_2;  // AND_Gate and_1, 32 bits wide
  _32bit_comparator u_32bit_comparator_1 (
    .in_1(in_1), .in_2(in_2), .out_3(n32bit_comparator_1_out_3), .out_4(n32bit_comparator_1_out_4),
    .out_5(n32bit_comparator_1_out_5));
  assign xor_1_out = in_1 ^ in_1;  // XOR_Gate xor_1, 32 bits wide
  assign or_2_out = n32bit_comparator_1_out_3 | n32bit_comparator_1_out_4 | n32bit_comparator_1_out_5;  // OR_Gate or_2, 32 bits wide
  _4_to_1_mux u_4_to_1_mux_1 (
    .in_1(adder_1_out), .in_2(subtractor_1_out), .in_3(or_1_out), .in_4(and_1_out), .out_12(out_6),
    .in_9(in_5), .in_10(in_4), .in_11(in_3), .in_5(or_2_out), .in_6(xor_1_out));  // open: in_7, in_8
endmodule

module _4_to_1_mux (
  input  [31:0] in_1,
  input  [31:0] in_2,
  input  [31:0] in_3,
  input  [31:0] in_4,
  input  [31:0] in_5,
  input  [31:0] in_6,
  input  [31:0] in_7,
  input  [31:0] in_8,
  input  [31:0] in_9,
  input  [31:0] in_10,
  input  [31:0] in_11,
  output [31:0] out_12
);

  wire [31:0] and_1_out, and_2_out, and_3_out, and_4_out, and_5_out, and_6_out, and_7_out, and_8_out,
       not_1_out, not_2_out, not_3_out;

  assign not_1_out = ~in_9;  // NOT_Gate not_1, 32 bits wide
  assign not_2_out = ~in_10;  // NOT_Gate not_2, 32 bits wide
  assign not_3_out = ~in_2;  // NOT_Gate not_3, 32 bits wide
  assign and_1_out = in_1 & not_3_out & not_2_out & not_1_out;  // AND_Gate and_1, 32 bits wide
  assign and_2_out = in_2 & in_2 & not_2_out & not_1_out;  // AND_Gate and_2, 32 bits wide
  assign and_3_out = in_3 & not_3_out & in_10 & not_1_out;  // AND_Gate and_3, 32 bits wide
  assign and_4_out = in_4 & in_2 & in_10 & not_1_out;  // AND_Gate and_4, 32 bits wide
  assign and_5_out = in_5 & not_3_out & not_2_out & in_9;  // AND_Gate and_5, 32 bits wide
  assign and_6_out = in_6 & in_2 & not_2_out & in_9;  // AND_Gate and_6, 32 bits wide
  assign and_7_out = in_7 & not_3_out & in_2 & in_9;  // AND_Gate and_7, 32 bits wide
  assign and_8_out = in_8 & in_2 & in_10 & in_9;  // AND_Gate and_8, 32 bits wide
  assign out_12 = and_1_out | and_4_out | and_5_out | and_2_out | and_3_out | and_7_out | and_6_out | and_8_out;  // OR_Gate or_1, 32 bits wide

  assign in_11 = in_2;

  // Notes on the sheet:
  //   d1
  //   d2
  //   d3
  //   d4
  //   d5
  //   d6
  //   d7
  //   d8
  //   s1
  //   s2
  //   s3
endmodule

module _32bit_comparator (
  input  [31:0] in_1,
  input  [31:0] in_2,
  output [31:0] out_3,
  output [31:0] out_4,
  output [31:0] out_5
);

  wire [31:0] not_1_out, not_2_out;

  assign not_1_out = ~in_1;  // NOT_Gate not_1, 32 bits wide
  assign not_2_out = ~in_2;  // NOT_Gate not_2, 32 bits wide
  assign out_3 = not_1_out & in_2;  // AND_Gate and_1, 32 bits wide
  assign out_5 = in_1 & not_2_out;  // AND_Gate and_2, 32 bits wide
  assign out_4 = ~(out_3 | out_5);  // NOR_Gate nor_1, 32 bits wide

  // Notes on the sheet:
  //   a>b
  //   a,b
  //   a=b
endmodule
