// Logisim project b;a.circ as structural Verilog: 1 circuit, main circuit main
module main (
  input  [4:0] in_1,
  input  [4:0] in_2
);

  wire [4:0] demultiplexer_2_out0, demultiplexer_2_out1, demultiplexer_2_out2, demultiplexer_2_out3,
       demultiplexer_2_out4, demultiplexer_2_out5, demultiplexer_2_out6, demultiplexer_2_out7,
       demultiplexer_2_out8, demultiplexer_2_out9, demultiplexer_2_out10, demultiplexer_2_out11,
       demultiplexer_2_out12, demultiplexer_2_out13, demultiplexer_2_out14, demultiplexer_2_out15;

  Demultiplexer #(.select(4), .width(5)) demultiplexer_1 (.in(in_2));  // open: out0, out1, out2, out3, out4, out5, out6, out7, out8, out9, out10, out11, out12, out13, out14, out15, sel, en
  Demultiplexer #(.select(4), .width(5)) demultiplexer_2 (
    .out0(demultiplexer_2_out0), .out1(demultiplexer_2_out1), .out2(demultiplexer_2_out2),
    .out3(demultiplexer_2_out3), .out4(demultiplexer_2_out4), .out5(demultiplexer_2_out5),
    .out6(demultiplexer_2_out6), .out7(demultiplexer_2_out7), .out8(demultiplexer_2_out8),
    .out9(demultiplexer_2_out9), .out10(demultiplexer_2_out10), .out11(demultiplexer_2_out11),
    .out12(demultiplexer_2_out12), .out13(demultiplexer_2_out13), .out14(demultiplexer_2_out14),
    .out15(demultiplexer_2_out15), .in(in_1));  // open: sel, en
  Register #(.width(32)) register_1 (.en(demultiplexer_2_out8[1]));  // open: D, Q, clk, clr
  Register #(.width(32)) register_2 (.D({32{1'b0}}), .en(demultiplexer_2_out0[1]));  // open: Q, clk, clr
  Register #(.width(32)) register_3 (.en(demultiplexer_2_out9[1]));  // open: D, Q, clk, clr
  Register #(.width(32)) register_4 ();  // open: D, en, Q, clk, clr
  Register #(.width(32)) register_5 ();  // open: D, en, Q, clk, clr
  Register #(.width(32)) register_6 ();  // open: D, en, Q, clk, clr
  Register #(.width(32)) register_7 (.en(demultiplexer_2_out1[1]));  // open: D, Q, clk, clr
  Register #(.width(32)) register_8 (.en(demultiplexer_2_out10[1]));  // open: D, Q, clk, clr
  Register #(.width(32)) register_9 ();  // open: D, en, Q, clk, clr
  Register #(.width(32)) register_10 ();  // open: D, en, Q, clk, clr
  Register #(.width(32)) register_11 (.en(demultiplexer_2_out2[1]));  // open: D, Q, clk, clr
  Register #(.width(32)) register_12 (.en(demultiplexer_2_out3[1]));  // open: D, Q, clk, clr
  Register #(.width(32)) register_13 ();  // open: D, en, Q, clk, clr
  Register #(.width(32)) register_14 ();  // open: D, en, Q, clk, clr
  Register #(.width(32)) register_15 ();  // open: D, en, Q, clk, clr
  Register #(.width(32)) register_16 ();  // open: D, en, Q, clk, clr
  Register #(.width(32)) register_17 (.en(demultiplexer_2_out4[1]));  // open: D, Q, clk, clr
  Register #(.width(32)) register_18 ();  // open: D, en, Q, clk, clr
  Register #(.width(32)) register_19 ();  // open: D, en, Q, clk, clr
  Register #(.width(32)) register_20 ();  // open: D, en, Q, clk, clr
  Register #(.width(32)) register_21 (.en(demultiplexer_2_out5[1]));  // open: D, Q, clk, clr
  Register #(.width(32)) register_22 ();  // open: D, en, Q, clk, clr
  Register #(.width(32)) register_23 ();  // open: D, en, Q, clk, clr
  Register #(.width(32)) register_24 ();  // open: D, en, Q, clk, clr
  Register #(.width(32)) register_25 ();  // open: D, en, Q, clk, clr
  Register #(.width(32)) register_26 (.en(demultiplexer_2_out6[1]));  // open: D, Q, clk, clr
  Register #(.width(32)) register_27 ();  // open: D, en, Q, clk, clr
  Register #(.width(32)) register_28 ();  // open: D, en, Q, clk, clr
  Register #(.width(32)) register_29 ();  // open: D, en, Q, clk, clr
  Register #(.width(32)) register_30 ();  // open: D, en, Q, clk, clr
  Register #(.width(32)) register_31 (.en(demultiplexer_2_out7[1]));  // open: D, Q, clk, clr
  Register #(.width(32)) register_32 ();  // open: D, en, Q, clk, clr
endmodule
