// Logisim project counter.circ as structural Verilog: 1 circuit, main circuit main
module main (
  output out_1,
  output out_2
);

  wire clock_1_out, d_ff_1_qn, d_ff_2_qn, not_1_out;

  Clock clock_1 (.out(clock_1_out));
  not not_1 (not_1_out, clock_1_out);
  D_Flip_Flop d_ff_1 (.clk(not_1_out), .D(d_ff_1_qn), .Q(out_2), .Qn(d_ff_1_qn));  // open: preset, en, reset
  D_Flip_Flop d_ff_2 (.clk(d_ff_1_qn), .D(d_ff_2_qn), .Q(out_1), .Qn(d_ff_2_qn));  // open: preset, en, reset
endmodule
