// Logisim project fetch unit.circ as structural Verilog: 1 circuit, main circuit main
module main (
  input  in_1,
  output [23:0] out_2
);

  wire clock_1_out;
  wire [7:0] register_1_q;
  wire [31:0] adder_1_out;

  Clock clock_1 (.out(clock_1_out));
  Register #(.width(32)) register_1 (
    .D(adder_1_out), .Q({register_1_q[7:2], out_2, register_1_q[1:0]}), .clk(clock_1_out), .clr(in_1));  // open: en
  Adder #(.width(32)) adder_1 (
    .a({register_1_q[7:2], out_2, register_1_q[1:0]}), .b(32'h4), .out(adder_1_out));  // open: cin, cout
  ROM #(.addrWidth(24), .dataWidth(32)) rom_1 (.addr(out_2));  // open: data, sel
endmodule
