// Logisim project lw and sw.circ as structural Verilog: 2 circuits, main circuit lw and sw
module lw_and_sw (
  input  [31:0] in_1,
  input  in_2
);

  wire control_unit_1_out_3, control_unit_1_out_4, decoder_1_p3, decoder_1_p5, decoder_1_p6,
       n32_bit_alu_1_p1, or_1_out, or_2_out;
  wire [2:0] decoder_1_p4;
  wire [6:0] decoder_1_p2, decoder_1_p7;
  wire [20:0] decoder_1_p8;
  wire [31:0] bit_extender_1_out, main_1_p3, multiplexer_1_out, n32_bit_alu_1_p4, n32_bit_alu_1_p5;

  // Decoder decoder_1: pin names not known; wires that end beside it: in_1, decoder_1_p2, decoder_1_p3, decoder_1_p4, decoder_1_p5, decoder_1_p6, decoder_1_p7, decoder_1_p8
  control_unit control_unit_1 (
    .opcode(decoder_1_p2), .out_3(control_unit_1_out_3), .out_4(control_unit_1_out_4));  // open: out_2, out_5, out_6, out_7
  assign bit_extender_1_out = {{11{1'b0}}, decoder_1_p8};  // Bit_Extender bit_extender_1
  Multiplexer #(.width(32)) multiplexer_1 (
    .in0(main_1_p3), .in1(bit_extender_1_out), .out(multiplexer_1_out), .sel(or_1_out));  // open: en
  or or_1 (or_1_out, control_unit_1_out_4, control_unit_1_out_3);
  // _32_bit_ALU 32_bit_alu_1: pin names not known; wires that end beside it: n32_bit_alu_1_p1, multiplexer_1_out, {decoder_1_p7[0], decoder_1_p4}, n32_bit_alu_1_p4, n32_bit_alu_1_p5, decoder_1_p3, in_2
  // Register_File_main main_1: pin names not known; wires that end beside it: n32_bit_alu_1_p1, decoder_1_p5, main_1_p3, decoder_1_p6
  or or_2 (or_2_out, control_unit_1_out_4, control_unit_1_out_3);
  RAM #(.addrWidth(24), .dataWidth(32), .bus("separate")) ram_1 (
    .addr(n32_bit_alu_1_p4[23:0]), .din(main_1_p3), .data(n32_bit_alu_1_p5), .str(control_unit_1_out_4),
    .sel(or_2_out), .ld(control_unit_1_out_3));  // open: clk, clr
endmodule

module control_unit (
  input  [6:0] opcode,
  output out_2,
  output out_3,
  output out_4,
  output out_5,
  output out_6,
  output out_7
);

  wire [2:0] type_1_p2;
  wire [31:0] bit_extender_1_out;

  assign bit_extender_1_out = {{25{1'b0}}, opcode};  // Bit_Extender bit_extender_1
  Demultiplexer #(.select(3)) demultiplexer_1 (
    .out1(out_2), .out2(out_3), .out3(out_4), .out4(out_5), .out5(out_6), .out6(out_7), .in(1'b1),
    .sel(type_1_p2));  // open: out0, out7, en
  // Type type_1: pin names not known; wires that end beside it: bit_extender_1_out, type_1_p2
endmodule
