// Logisim project mux.circ as structural Verilog: 3 circuits, main circuit main
module main (
  input  in_1,
  input  in_2,
  input  in_3,
  input  in_4,
  input  in_5,
  input  in_6,
  output out_7
);

  wire mux_1_out_4, mux_2_out_4;

  mux mux_1 (.I1(in_2), .A(in_6), .I0(in_1), .out_4(mux_1_out_4));
  mux mux_2 (.I1(in_4), .A(in_6), .I0(in_3), .out_4(mux_2_out_4));
  mux mux_3 (.I1(mux_2_out_4), .A(in_5), .I0(mux_1_out_4), .out_4(out_7));

  // Notes on the sheet:
  //   I1
  //   I0
  //   I1
  //   Ia
endmodule

module mux (
  input  I1,
  input  A,
  input  I0,
  output out_4
);

  wire nand_1_out, nand_2_out, nand_3_out;

  nand nand_1 (nand_1_out, A, A);
  nand nand_2 (nand_2_out, I1, A);
  nand nand_3 (nand_3_out, nand_1_out, I0);
  nand nand_4 (out_4, nand_2_out, nand_3_out);
endmodule

module mux_v2 (
  input  I1,
  input  A,
  input  in_3,
  input  in_4,
  input  in_5,
  input  in_6,
  output out_7,
  output out_8
);

  wire nand_1_out, nand_2_out, nand_3_out, nand_4_out, nand_5_out, nand_6_out;

  nand nand_1 (nand_1_out, A, A);
  nand nand_2 (nand_2_out, in_5, in_5);
  nand nand_3 (nand_3_out, I1, A);
  nand nand_4 (nand_4_out, nand_1_out, in_3);
  nand nand_5 (nand_5_out, in_4, in_5);
  nand nand_6 (nand_6_out, nand_2_out, in_6);
  nand nand_7 (out_7, nand_3_out, nand_4_out);
  nand nand_8 (out_8, nand_5_out, nand_6_out);
endmodule
