// Logisim project nla2.circ as structural Verilog: 2 circuits, main circuit main
module main (
  input  [31:0] in_1,
  input  [3:0] in_2,
  input  [31:0] in_3,
  output [31:0] out_4
);

  wire [31:0] adder_1_out, and_1_out, comp_1_out_3, comp_1_out_4, comp_1_out_5, divider_1_out,
       multiplier_1_out, or_1_out, or_2_out, shifter_1_out, shifter_2_out, shifter_3_out, subtractor_1_out,
       xor_1_out;

  Adder #(.width(32)) adder_1 (.a(in_1), .b(in_3), .out(adder_1_out));  // open: cin, cout
  Subtractor #(.width(32)) subtractor_1 (.a(in_1), .b(in_3), .out(subtractor_1_out));  // open: bin, bout
  assign or_1_out = in_1 | in_3;  // OR_Gate or_1, 32 bits wide
  assign and_1_out = in_1 & in_3;  // AND_Gate and_1, 32 bits wide
  comp comp_1 (.in_1(in_1), .in_2(in_3), .out_3(comp_1_out_3), .out_4(comp_1_out_4), .out_5(comp_1_out_5));
  assign xor_1_out = in_1 ^ in_1;  // XOR_Gate xor_1, 32 bits wide
  Shifter #(.width(32)) shifter_1 (.in(in_1), .\dist (in_3[31:27]), .out(shifter_1_out));
  Shifter #(.width(32), .shift("lr")) shifter_2 (.in(in_1), .\dist (in_3[31:27]), .out(shifter_2_out));
  Shifter #(.width(32), .shift("ar")) shifter_3 (.in(in_1), .\dist (in_3[31:27]), .out(shifter_3_out));
  Multiplier #(.width(32)) multiplier_1 (.out(multiplier_1_out));  // open: a, b, cin, cout
  Divider #(.width(32)) divider_1 (.out(divider_1_out));  // open: a, b, upper, rem
  assign or_2_out = comp_1_out_3 | comp_1_out_4 | comp_1_out_5;  // OR_Gate or_2, 32 bits wide
  Multiplexer #(.select(4), .width(32)) multiplexer_1 (
    .in0(adder_1_out), .in1(subtractor_1_out), .in2(or_1_out), .in3(and_1_out), .in4(or_2_out),
    .in5(xor_1_out), .in6(shifter_1_out), .in7(shifter_2_out), .in8(shifter_3_out), .in9(multiplier_1_out),
    .in10(divider_1_out), .out(out_4), .sel(in_2));  // open: in11, in12, in13, in14, in15, en
endmodule

module comp (
  input  [31:0] in_1,
  input  [31:0] in_2,
  output [31:0] out_3,
  output [31:0] out_4,
  output [31:0] out_5
);

  wire [31:0] not_1_out, not_2_out;

  assign not_1_out = ~in_1;  // NOT_Gate not_1, 32 bits wide
  assign not_2_out = ~in_2;  // NOT_Gate not_2, 32 bits wide
  assign out_3 = not_1_out & in_2;  // AND_Gate and_1, 32 bits wide
  assign out_5 = in_1 & not_2_out;  // AND_Gate and_2, 32 bits wide
  assign out_4 = ~(out_3 | out_5);  // NOR_Gate nor_1, 32 bits wide

  // Notes on the sheet:
  //   a>b
  //   a,b
  //   a=b
endmodule
