// Logisim project register file.circ as structural Verilog: 1 circuit, main circuit main
module main (
  input  [4:0] in_1,
  input  [4:0] in_2,
  input  [4:0] in_3,
  input  [31:0] in_4,
  input  in_5,
  input  Clock_cycle,
  input  in_7,
  output [31:0] out_8,
  output [31:0] out_9
);

  wire decoder_1_out0, decoder_1_out1, decoder_1_out2, decoder_1_out3, decoder_1_out4, decoder_1_out5,
       decoder_1_out6, decoder_1_out7, decoder_1_out8, decoder_1_out9, decoder_1_out10, decoder_1_out11,
       decoder_1_out12, decoder_1_out13, decoder_1_out14, decoder_1_out15, decoder_1_out16, decoder_1_out17,
       decoder_1_out18, decoder_1_out19, decoder_1_out20, decoder_1_out21, decoder_1_out22, decoder_1_out23,
       decoder_1_out24, decoder_1_out25, decoder_1_out26, decoder_1_out27, decoder_1_out28, decoder_1_out29,
       decoder_1_out30, decoder_1_out31;
  wire [31:0] demultiplexer_1_out0, demultiplexer_1_out1, demultiplexer_1_out2, demultiplexer_1_out3,
       demultiplexer_1_out4, demultiplexer_1_out5, demultiplexer_1_out6, demultiplexer_1_out7,
       demultiplexer_1_out8, demultiplexer_1_out9, demultiplexer_1_out10, demultiplexer_1_out11,
       demultiplexer_1_out12, demultiplexer_1_out13, demultiplexer_1_out14, demultiplexer_1_out15,
       demultiplexer_1_out16, demultiplexer_1_out17, demultiplexer_1_out18, demultiplexer_1_out19,
       demultiplexer_1_out20, demultiplexer_1_out21, demultiplexer_1_out22, demultiplexer_1_out23,
       demultiplexer_1_out24, demultiplexer_1_out25, demultiplexer_1_out26, demultiplexer_1_out27,
       demultiplexer_1_out28, demultiplexer_1_out29, demultiplexer_1_out30, demultiplexer_1_out31,
       register_1_q, register_2_q, register_3_q, register_4_q, register_5_q, register_6_q, register_7_q,
       register_8_q, register_9_q, register_10_q, register_11_q, register_12_q, register_13_q, register_14_q,
       register_15_q, register_16_q, register_17_q, register_18_q, register_19_q, register_20_q,
       register_21_q, register_22_q, register_23_q, register_24_q, register_25_q, register_26_q,
       register_27_q, register_28_q, register_29_q, register_30_q, register_31_q, register_32_q;

  Demultiplexer #(.select(5), .width(32)) demultiplexer_1 (
    .out0(demultiplexer_1_out0), .out1(demultiplexer_1_out1), .out2(demultiplexer_1_out2),
    .out3(demultiplexer_1_out3), .out4(demultiplexer_1_out4), .out5(demultiplexer_1_out5),
    .out6(demultiplexer_1_out6), .out7(demultiplexer_1_out7), .out8(demultiplexer_1_out8),
    .out9(demultiplexer_1_out9), .out10(demultiplexer_1_out10), .out11(demultiplexer_1_out11),
    .out12(demultiplexer_1_out12), .out13(demultiplexer_1_out13), .out14(demultiplexer_1_out14),
    .out15(demultiplexer_1_out15), .out16(demultiplexer_1_out16), .out17(demultiplexer_1_out17),
    .out18(demultiplexer_1_out18), .out19(demultiplexer_1_out19), .out20(demultiplexer_1_out20),
    .out21(demultiplexer_1_out21), .out22(demultiplexer_1_out22), .out23(demultiplexer_1_out23),
    .out24(demultiplexer_1_out24), .out25(demultiplexer_1_out25), .out26(demultiplexer_1_out26),
    .out27(demultiplexer_1_out27), .out28(demultiplexer_1_out28), .out29(demultiplexer_1_out29),
    .out30(demultiplexer_1_out30), .out31(demultiplexer_1_out31), .in(in_4), .sel(in_3), .en(in_5));
  Decoder #(.select(5)) decoder_1 (
    .out0(decoder_1_out0), .out1(decoder_1_out1), .out2(decoder_1_out2), .out3(decoder_1_out3),
    .out4(decoder_1_out4), .out5(decoder_1_out5), .out6(decoder_1_out6), .out7(decoder_1_out7),
    .out8(decoder_1_out8), .out9(decoder_1_out9), .out10(decoder_1_out10), .out11(decoder_1_out11),
    .out12(decoder_1_out12), .out13(decoder_1_out13), .out14(decoder_1_out14), .out15(decoder_1_out15),
    .out16(decoder_1_out16), .out17(decoder_1_out17), .out18(decoder_1_out18), .out19(decoder_1_out19),
    .out20(decoder_1_out20), .out21(decoder_1_out21), .out22(decoder_1_out22), .out23(decoder_1_out23),
    .out24(decoder_1_out24), .out25(decoder_1_out25), .out26(decoder_1_out26), .out27(decoder_1_out27),
    .out28(decoder_1_out28), .out29(decoder_1_out29), .out30(decoder_1_out30), .out31(decoder_1_out31),
    .sel(in_3), .en(in_5));
  Register #(.width(32)) register_1 (
    .D({32{1'b0}}), .en(decoder_1_out0), .Q(register_1_q), .clk(in_7), .clr(Clock_cycle));
  Register #(.width(32)) register_2 (
    .D(demultiplexer_1_out2), .en(decoder_1_out2), .Q(register_2_q), .clk(in_7), .clr(Clock_cycle));
  Register #(.width(32)) register_3 (
    .D(demultiplexer_1_out4), .en(decoder_1_out4), .Q(register_3_q), .clk(in_7), .clr(Clock_cycle));
  Register #(.width(32)) register_4 (
    .D(demultiplexer_1_out6), .en(decoder_1_out6), .Q(register_4_q), .clk(in_7), .clr(Clock_cycle));
  Register #(.width(32)) register_5 (
    .D(demultiplexer_1_out8), .en(decoder_1_out8), .Q(register_5_q), .clk(in_7), .clr(Clock_cycle));
  Register #(.width(32)) register_6 (
    .D(demultiplexer_1_out10), .en(decoder_1_out10), .Q(register_6_q), .clk(in_7), .clr(Clock_cycle));
  Register #(.width(32)) register_7 (
    .D(demultiplexer_1_out12), .en(decoder_1_out12), .Q(register_7_q), .clk(in_7), .clr(Clock_cycle));
  Register #(.width(32)) register_8 (
    .D(demultiplexer_1_out14), .en(decoder_1_out14), .Q(register_8_q), .clk(in_7), .clr(Clock_cycle));
  Register #(.width(32)) register_9 (
    .D(demultiplexer_1_out16), .en(decoder_1_out16), .Q(register_9_q), .clk(in_7), .clr(Clock_cycle));
  Register #(.width(32)) register_10 (
    .D(demultiplexer_1_out18), .en(decoder_1_out18), .Q(register_10_q), .clk(in_7), .clr(Clock_cycle));
  Register #(.width(32)) register_11 (
    .D(demultiplexer_1_out20), .en(decoder_1_out20), .Q(register_11_q), .clk(in_7), .clr(Clock_cycle));
  Register #(.width(32)) register_12 (
    .D(demultiplexer_1_out22), .en(decoder_1_out22), .Q(register_12_q), .clk(in_7), .clr(Clock_cycle));
  Register #(.width(32)) register_13 (
    .D(demultiplexer_1_out24), .en(decoder_1_out24), .Q(register_13_q), .clk(in_7), .clr(Clock_cycle));
  Register #(.width(32)) register_14 (
    .D(demultiplexer_1_out26), .en(decoder_1_out26), .Q(register_14_q), .clk(in_7), .clr(Clock_cycle));
  Register #(.width(32)) register_15 (
    .D(demultiplexer_1_out28), .en(decoder_1_out28), .Q(register_15_q), .clk(in_7), .clr(Clock_cycle));
  Register #(.width(32)) register_16 (
    .D(demultiplexer_1_out30), .en(decoder_1_out30), .Q(register_16_q), .clk(in_7), .clr(Clock_cycle));
  Register #(.width(32)) register_17 (
    .D(demultiplexer_1_out1), .en(decoder_1_out1), .Q(register_17_q), .clk(in_7), .clr(Clock_cycle));
  Register #(.width(32)) register_18 (
    .D(demultiplexer_1_out3), .en(decoder_1_out3), .Q(register_18_q), .clk(in_7), .clr(Clock_cycle));
  Register #(.width(32)) register_19 (
    .D(demultiplexer_1_out5), .en(decoder_1_out5), .Q(register_19_q), .clk(in_7), .clr(Clock_cycle));
  Register #(.width(32)) register_20 (
    .D(demultiplexer_1_out7), .en(decoder_1_out7), .Q(register_20_q), .clk(in_7), .clr(Clock_cycle));
  Register #(.width(32)) register_21 (
    .D(demultiplexer_1_out9), .en(decoder_1_out9), .Q(register_21_q), .clk(in_7), .clr(Clock_cycle));
  Register #(.width(32)) register_22 (
    .D(demultiplexer_1_out11), .en(decoder_1_out11), .Q(register_22_q), .clk(in_7), .clr(Clock_cycle));
  Register #(.width(32)) register_23 (
    .D(demultiplexer_1_out13), .en(decoder_1_out13), .Q(register_23_q), .clk(in_7), .clr(Clock_cycle));
  Register #(.width(32)) register_24 (
    .D(demultiplexer_1_out15), .en(decoder_1_out15), .Q(register_24_q), .clk(in_7), .clr(Clock_cycle));
  Register #(.width(32)) register_25 (
    .D(demultiplexer_1_out17), .en(decoder_1_out17), .Q(register_25_q), .clk(in_7), .clr(Clock_cycle));
  Register #(.width(32)) register_26 (
    .D(demultiplexer_1_out19), .en(decoder_1_out19), .Q(register_26_q), .clk(in_7), .clr(Clock_cycle));
  Register #(.width(32)) register_27 (
    .D(demultiplexer_1_out21), .en(decoder_1_out21), .Q(register_27_q), .clk(in_7), .clr(Clock_cycle));
  Register #(.width(32)) register_28 (
    .D(demultiplexer_1_out23), .en(decoder_1_out23), .Q(register_28_q), .clk(in_7), .clr(Clock_cycle));
  Register #(.width(32)) register_29 (
    .D(demultiplexer_1_out25), .en(decoder_1_out25), .Q(register_29_q), .clk(in_7), .clr(Clock_cycle));
  Register #(.width(32)) register_30 (
    .D(demultiplexer_1_out27), .en(decoder_1_out27), .Q(register_30_q), .clk(in_7), .clr(Clock_cycle));
  Register #(.width(32)) register_31 (
    .D(demultiplexer_1_out29), .en(decoder_1_out29), .Q(register_31_q), .clk(in_7), .clr(Clock_cycle));
  Register #(.width(32)) register_32 (
    .D(demultiplexer_1_out31), .en(decoder_1_out31), .Q(register_32_q), .clk(in_7), .clr(Clock_cycle));
  Multiplexer #(.select(5), .width(32), .enable("false")) multiplexer_1 (
    .in0(register_1_q), .in1(register_17_q), .in2(register_2_q), .in3(register_18_q), .in4(register_3_q),
    .in5(register_19_q), .in6(register_4_q), .in7(register_20_q), .in8(register_5_q), .in9(register_21_q),
    .in10(register_6_q), .in11(register_22_q), .in12(register_7_q), .in13(register_23_q),
    .in14(register_8_q), .in15(register_24_q), .in16(register_9_q), .in17(register_25_q),
    .in18(register_10_q), .in19(register_26_q), .in20(register_11_q), .in21(register_27_q),
    .in22(register_12_q), .in23(register_28_q), .in24(register_13_q), .in25(register_29_q),
    .in26(register_14_q), .in27(register_30_q), .in28(register_15_q), .in29(register_31_q),
    .in30(register_16_q), .in31(register_32_q), .out(out_8), .sel(in_1));
  Multiplexer #(.select(5), .width(32), .enable("false")) multiplexer_2 (
    .in0(register_1_q), .in1(register_17_q), .in2(register_2_q), .in3(register_18_q), .in4(register_3_q),
    .in5(register_19_q), .in6(register_4_q), .in7(register_20_q), .in8(register_5_q), .in9(register_21_q),
    .in10(register_6_q), .in11(register_22_q), .in12(register_7_q), .in13(register_23_q),
    .in14(register_8_q), .in15(register_24_q), .in16(register_9_q), .in17(register_25_q),
    .in18(register_10_q), .in19(register_26_q), .in20(register_11_q), .in21(register_27_q),
    .in22(register_12_q), .in23(register_28_q), .in24(register_13_q), .in25(register_29_q),
    .in26(register_14_q), .in27(register_30_q), .in28(register_15_q), .in29(register_31_q),
    .in30(register_16_q), .in31(register_32_q), .out(out_9), .sel(in_2));

  // Notes on the sheet:
  //   Address of Source Register 1
  //   Address of Source Register 2
  //   Address of Destination Register
  //   Write back to Destination Register
  //   Write back switch enable
  //   Reset data of register
  //   Data of rs1
  //   Data of rs2
endmodule
