// Logisim project w2.circ as structural Verilog: 2 circuits, main circuit main
module main (
  input  in_1,
  input  in_2,
  output out_3,
  output out_4,
  output out_5
);

  comparator comparator_1 (.A(in_2), .B(in_1), .A___B(out_3), .A___B_2(out_4), .A___B_3(out_5));

  // Notes on the sheet:
  //   A
  //   B
endmodule

module comparator (
  input  A,
  input  B,
  output A___B,
  output A___B_2,
  output A___B_3
);

  wire not_1_out, not_2_out;

  not not_1 (not_1_out, B);
  not not_2 (not_2_out, A);
  and and_1 (A___B, A, not_1_out);
  xnor xnor_1 (A___B_2, A, B);
  and and_2 (A___B_3, B, not_2_out);
endmodule
