// Logisim project w3.circ as structural Verilog: 3 circuits, main circuit main
module main (
  input  in_1,
  output out_2
);

  wire clock_1_out, d_ff_1_q, d_ff_2_q, d_ff_3_q, d_flipflop_1_out_3, d_flipflop_2_out_3, d_flipflop_3_out_3,
       not_1_out;

  Clock clock_1 (.out(clock_1_out));
  not not_1 (not_1_out, in_1);
  D_Flip_Flop d_ff_1 (.clk(not_1_out), .D(clock_1_out), .Q(d_ff_1_q));  // open: Qn, preset, en, reset
  D_Flip_Flop d_ff_2 (.clk(d_ff_1_q), .D(clock_1_out), .Q(d_ff_2_q));  // open: Qn, preset, en, reset
  D_flipflop d_flipflop_1 (.D(clock_1_out), .CLK(clock_1_out), .out_3(d_flipflop_1_out_3));  // open: out_4
  D_Flip_Flop d_ff_3 (.clk(d_ff_2_q), .D(clock_1_out), .Q(d_ff_3_q));  // open: Qn, preset, en, reset
  D_Flip_Flop d_ff_4 (.clk(d_ff_3_q), .D(clock_1_out));  // open: Q, Qn, preset, en, reset
  D_flipflop d_flipflop_2 (.D(d_flipflop_1_out_3), .CLK(clock_1_out), .out_3(d_flipflop_2_out_3));  // open: out_4
  D_flipflop d_flipflop_3 (.D(d_flipflop_2_out_3), .CLK(clock_1_out), .out_3(d_flipflop_3_out_3));  // open: out_4
  D_flipflop d_flipflop_4 (.D(d_flipflop_3_out_3), .CLK(clock_1_out), .out_3(out_2));  // open: out_4

  // Notes on the sheet:
  //   Serial in serial Out
endmodule

module D_flipflop (
  input  D,
  input  CLK,
  output out_3,
  output out_4
);

  wire nand_1_out, nand_2_out;

  nand nand_1 (nand_1_out, D, CLK);
  nand nand_2 (nand_2_out, nand_1_out, CLK);
  nand nand_3 (out_3, nand_1_out, out_4);
  nand nand_4 (out_4, out_3, nand_2_out);

  // Notes on the sheet:
  //   R
  //   S
endmodule

module \new  (
  input  in_1,
  input  in_2,
  input  in_3,
  input  in_4,
  input  in_5
);

  wire clock_1_out;

  Clock clock_1 (.out(clock_1_out));
  D_flipflop d_flipflop_1 (.D(in_1), .CLK(clock_1_out), .out_3(in_3));  // open: out_4
  D_flipflop d_flipflop_2 (.D(in_3), .CLK(clock_1_out), .out_3(in_5));  // open: out_4
  D_flipflop d_flipflop_3 (.D(in_5), .CLK(clock_1_out), .out_3(in_4));  // open: out_4
  D_flipflop d_flipflop_4 (.D(in_4), .CLK(clock_1_out), .out_3(in_2));  // open: out_4
endmodule
