// Logisim project w4.circ as structural Verilog: 1 circuit, main circuit main
module main (
);

  wire clock_1_out;

  Clock clock_1 (.out(clock_1_out));
  D_Flip_Flop d_ff_1 (.D(clock_1_out));  // open: clk, Q, Qn, preset, en, reset
  D_Flip_Flop d_ff_2 (.D(clock_1_out));  // open: clk, Q, Qn, preset, en, reset
  D_Flip_Flop d_ff_3 (.D(clock_1_out));  // open: clk, Q, Qn, preset, en, reset
  D_Flip_Flop d_ff_4 (.D(clock_1_out));  // open: clk, Q, Qn, preset, en, reset
endmodule
