// Logisim project w6.circ as structural Verilog: 1 circuit, main circuit main
module main (
  input  [31:0] in_1,
  input  [31:0] in_2,
  output [31:0] out_3,
  output [31:0] out_4,
  output [31:0] out_5
);

  wire [31:0] not_1_out, not_2_out;

  assign not_1_out = ~in_1;  // NOT_Gate not_1, 32 bits wide
  assign not_2_out = ~in_2;  // NOT_Gate not_2, 32 bits wide
  assign out_3 = not_1_out & in_2;  // AND_Gate and_1, 32 bits wide
  assign out_5 = in_1 & not_2_out;  // AND_Gate and_2, 32 bits wide
  assign out_4 = ~(out_3 | out_5);  // NOR_Gate nor_1, 32 bits wide

  // Notes on the sheet:
  //   a<b
  //   a>b
  //   a=b
endmodule
